// Logisim project arquitetura.circ as structural Verilog: 1 circuit, main circuit main
module main (
  input  [7:0] matriz00,
  input  [7:0] matriz01,
  input  [7:0] matriz02,
  input  [7:0] matriz10,
  input  [7:0] matriz11,
  input  [7:0] matriz12,
  input  [7:0] matriz20,
  input  [7:0] matriz21,
  input  [7:0] matriz22,
  input  in_10,
  output [7:0] out_11
);

  wire [7:0] adder_1_out, adder_2_out, adder_3_out, adder_4_out, multiplexer_1_out, multiplexer_2_out,
       multiplexer_3_out, multiplexer_4_out, multiplexer_5_out, not_1_out, not_2_out, register_1_q,
       shifter_1_out;

  Multiplexer #(.width(8)) multiplexer_1 (
    .in0(matriz00), .in1(matriz20), .out(multiplexer_1_out), .sel(in_10));  // open: en
  Multiplexer #(.width(8)) multiplexer_2 (
    .in0(matriz02), .in1(matriz22), .out(multiplexer_2_out), .sel(in_10));  // open: en
  Multiplexer #(.width(8)) multiplexer_3 (
    .in0(matriz01), .in1(matriz21), .out(multiplexer_3_out), .sel(in_10));  // open: en
  Adder adder_1 (.a(multiplexer_1_out), .b(multiplexer_2_out), .out(adder_1_out));  // open: cin, cout
  Shifter shifter_1 (.in(multiplexer_3_out), .\dist (3'b001), .out(shifter_1_out));
  assign not_1_out = ~adder_1_out;  // NOT_Gate not_1, 8 bits wide
  assign not_2_out = ~shifter_1_out;  // NOT_Gate not_2, 8 bits wide
  Adder adder_2 (.a(not_1_out), .b(8'h1), .out(adder_2_out));  // open: cin, cout
  Adder adder_3 (.a(not_2_out), .b(8'h1), .out(adder_3_out));  // open: cin, cout
  Multiplexer #(.width(8)) multiplexer_4 (
    .in0(adder_1_out), .in1(adder_2_out), .out(multiplexer_4_out), .sel(in_10));  // open: en
  Multiplexer #(.width(8)) multiplexer_5 (
    .in0(shifter_1_out), .in1(adder_3_out), .out(multiplexer_5_out), .sel(in_10));  // open: en
  Adder adder_4 (.a(multiplexer_4_out), .b(multiplexer_5_out), .out(adder_4_out));  // open: cin, cout
  Register register_1 (.D(adder_4_out), .Q(register_1_q), .clk(in_10));  // open: en, clr
  Adder adder_5 (.a(register_1_q), .b(adder_4_out), .out(out_11));  // open: cin, cout

  // Notes on the sheet:
  //   not_1 drives only 0 and floats otherwise
endmodule
